// Logisim project Bird.circ as structural Verilog
module Control_Unit (
  input  [3:0] in_1,
  output [8:0] out_2
);

  ROM #(.addrWidth(4), .dataWidth(9)) rom_1 (.addr(in_1), .data(out_2));  // open: sel

  // Other names for the same wires on the sheet: irld = out_2[0]; memld = out_2[1]; mux = out_2[2]; zfld = out_2[3];
  //   regld = out_2[4]; armux = out_2[5]; pcinc = out_2[6]; pcld = out_2[7]; fetch = out_2[8]

  // Notes on the sheet:
  //   Control Unit for Reptile     -      Including LD, ST, JUMP, JZ
  //   contents of rom_1 (hex, n*v repeats v):
  //   141 51 34 22 0 80 0 18
endmodule
